# Fritzing sketch pieman2 (saved by Fritzing 0.9.3b)
breadboards: 1

parts:
  S1 = Momentary Switch [package=ksa_sealed_tac_switch]
  S2 = Momentary Switch [package=ksa_sealed_tac_switch]
  S3 = Momentary Switch [package=ksa_sealed_tac_switch]
  S4 = Momentary Switch [package=ksa_sealed_tac_switch]
  LED1 = RGB LED (com. cathode, rbg) [package="5 mm [THT]"]
  Part2 = Tessel 2
  R7 = Resistor [tolerance=±5% resistance=100 package="0603 [SMD]"]
  R8 = Resistor [tolerance=±5% resistance=100 package="0603 [SMD]"]
  R9 = Resistor [tolerance=±5% resistance=100 package="0603 [SMD]"]
  R10 = Resistor [tolerance=±5% resistance=100 package="0603 [SMD]"]
  R11 = Resistor [tolerance=±5% resistance=100 package="0603 [SMD]"]

nets:
  N1: S1.1, R8.Pin_0, R9.Pin_1
  N2: S1.4, S2.4, S3.4, S4.4, LED1.common_cathode, Part2.GND
  N3: S2.1, R9.Pin_0, R10.Pin_1
  N4: S3.1, R10.Pin_0, R11.Pin_1
  N5: S4.1, R11.Pin_0
  N6: LED1.red_anode, Part2.6#76
  N7: LED1.blue_anode, Part2.5
  N8: LED1.green_anode, Part2.6#36
  N9: Part2.4, R7.Pin_0, R8.Pin_1

notes:
  Joining the buttons with resistors creates a voltage ladder. Instead of using the J5.Button component, use j5.Sensor.

custom parts:
  Tessel 2: Draft version of Tessel 2
